# Fritzing sketch diagrams (saved by Fritzing 0.9.4)
breadboards: 1

parts:
  Arduino = Arduino Uno (Rev3)
  1K = PHOTOCELL [package=photocell]
  LED1_IR = LEDs [package=led10mm]
  R1 = Resistor [tolerance=±5% resistance=1k package="0805 [SMD]"]
  R2 = Resistor [tolerance=±5% resistance=220 package="2512 [SMD]"]
  LASER_SENSOR = Camdenboss CTB0158-3 [package=THT]

nets (from the breadboard view):
  N1: Arduino.A0, 1K.P$1, R1.Pin_1
  N2: Arduino.D13/SCK, LED1_IR.A
  N3: Arduino.GND, 1K.P$2, R2.Pin_1, LASER_SENSOR.pin3
  N4: Arduino.D2, LASER_SENSOR.pin2
  N5: Arduino.5V, R1.Pin_0, LASER_SENSOR.pin1
  N6: LED1_IR.C, R2.Pin_0

notes:
  laser sensor
